// Digital circuit project05.dig as structural Verilog
module project05 (
  input  CLK,
  input  [3:0] PROG,
  input  CLR,
  output [7:0] DP,
  output [7:0] MEM,
  output [7:0] BR,
  output [7:0] MUL,
  output [7:0] BX,
  output [7:0] ICOUNT,
  output DONE
);

  wire and_1_out;

  and and_1 (and_1_out, CLK, ~DONE);  // And
  // _32bit_eq _32bit_eq_1: pin names not known; wires that end beside it: and_1_out, 32'he2800000, 32'he2800000, DONE

  assign BR = {8{1'b0}};
  assign BX = {8{1'b0}};
  assign DP = {8{1'b0}};
  assign ICOUNT = {8{1'b0}};
  assign MEM = {8{1'b0}};
  assign MUL = {8{1'b0}};

  // Notes on the sheet:
  //   Lengend
  //   0 - quadratic-s
  //   1 - sum-array-s
  //   2 - find-max-s
  //   3 - fact-s
  //   4 - fib-rec-s
  //   5 - stolower-s
endmodule
